# Fritzing sketch V2 Electrical schematics_Fritzing (saved by Fritzing 0.9.3b)

parts:
  Part1 = Arduino Nano (Rev3.0)
  Pololu_A1 = Pololu A4988 [package=SO16]
  U2 = POT_SWITCH [package=pot_pth_switch]
  U4 = SWITCH_SPDT [package=kps-1290]
  Part2 = Tri-Axis Gyro Breakout - L3G4200D
  M1 = Stepper Motor - Bipolar
  C4 = Electrolytic Capacitor [capacitance=100µF package="200 mil [THT, electrolytic]"]
  M3 = Stepper Motor - Bipolar
  C5 = Electrolytic Capacitor [capacitance=100µF package="200 mil [THT, electrolytic]"]
  Pololu_A2 = Pololu A4988 [package=SO16]
  F1 = FUSE [package=fuse_5mm]
  U5 = POT_SWITCH [package=pot_pth_switch]
  U6 = POT_SWITCH [package=pot_pth_switch]
  R1 = Resistor [tolerance=±5% resistance=220 package="1206 [SMD]"]
  R2 = Resistor [tolerance=±5% resistance=220 package="1206 [SMD]"]
  Part4 = LilyPad Coin Cell Battery Holder
  R4 = Resistor [tolerance=±5% resistance=220 package="1206 [SMD]"]
  Part5 = Bluetooth HC-05 Macho

nets:
  N1: Part1.D1/TX, Part5.TXD
  N2: Part1.D0/RX, Part5.RXD
  N3: Part1.RESET, Pololu_A1.ENABLE, Pololu_A2.ENABLE
  GND: Part1.GND, Pololu_A1.GND#8, U2.G$1_A, Pololu_A2.GND#8, U5.G$1_A, U6.G$1_A, R2.Pin_1, R4.Pin_1, Part5.GND
  N4: Part1.D2, Pololu_A2.DIR
  N5: Part1.D3, Pololu_A2.STEP
  N6: Part1.D4, Pololu_A1.DIR
  N7: Part1.D5, Pololu_A1.STEP
  N8: Part1.VIN, Pololu_A1.VMOT, U4.S, C4.-, C5.-, Pololu_A2.VMOT, R1.Pin_0
  VDD: Part1.5V, Pololu_A1.VDD, U2.G$2_2, Pololu_A2.VDD, U5.G$2_2, U6.G$2_2, Part5.VCC
  N9: Part1.A6, R1.Pin_1, R2.Pin_0, R4.Pin_0
  N10: Part1.A5, Part2.SCL
  N11: Part1.A4, Part2.SDA
  N12: Part1.A3, U5.G$2_1
  N13: Part1.A2, U2.G$2_1
  N14: Part1.A1, U6.G$2_1
  N15: Pololu_A1.MS1, Pololu_A1.MS2, Pololu_A1.MS3
  N16: Pololu_A1.RESET, Pololu_A1.SLEEP
  N17: Pololu_A1.1B, M1.D
  N18: Pololu_A1.1A, M1.B
  N19: Pololu_A1.2A, M1.C
  N20: Pololu_A1.2B, M1.A
  N21: Pololu_A1.GND#14, Part2.GND, C4.+, C5.+, Pololu_A2.GND#14, F1.1, Part4.-, Part4.+
  N22: U4.P, F1.2
  N23: M3.A, Pololu_A2.2B
  N24: M3.C, Pololu_A2.2A
  N25: M3.B, Pololu_A2.1A
  N26: M3.D, Pololu_A2.1B
  N27: Pololu_A2.MS1, Pololu_A2.MS2, Pololu_A2.MS3
  N28: Pololu_A2.RESET, Pololu_A2.SLEEP

notes:
  Li-Ion Battery 3S 10,8V (9,3~12,3V)
  1S - 3,6V (3,1~4.1V)x3
  Arduino Nano
  MPU-6050 Gyro
  Main switch
  2x Stepper motors
  2x Stepper motor driver with heatsink (up to 2A) + 100mF capacitor
  7A Fuse
  3x Potentiometer (10k Ohm) for easy PID tuning
  3x 200k Ohm Resistors for measuring battery voltage (1/3)
  Bluetooth module
